# Fritzing sketch CMStormProMicroDesign (saved by Fritzing 0.9.5d)
breadboards: 1

parts:
  SparkFun_Pro_Micro1 = SparkFun Pro Micro [part_number=DEV-12640]
  LED1 = LEDs [package=led10mm]
  LED2 = LEDs [package=led10mm]
  LED3 = LEDs [package=led10mm]
  LED4 = LEDs [package=led10mm]
  LED5 = LEDs [package=led10mm]
  LED6 = LEDs [package=led10mm]
  S1 = Pushbutton [part_number=COM-09190 package="[THT]"]
  S2 = Pushbutton [part_number=COM-09190 package="[THT]"]
  S3 = Pushbutton [part_number=COM-09190 package="[THT]"]
  S4 = Pushbutton [part_number=COM-09190 package="[THT]"]
  S5 = Pushbutton [part_number=COM-09190 package="[THT]"]
  S6 = Pushbutton [part_number=COM-09190 package="[THT]"]

nets:
  N1: SparkFun_Pro_Micro1.MOSI, LED1.A, LED2.A, LED3.A, LED4.A, LED5.A, LED6.A
  N2: SparkFun_Pro_Micro1.D7, S6.Pin_1, S6.Pin_2
  N3: SparkFun_Pro_Micro1.D6, S5.Pin_1, S5.Pin_2
  N4: SparkFun_Pro_Micro1.D5, S4.Pin_1, S4.Pin_2
  N5: SparkFun_Pro_Micro1.D4, S3.Pin_1, S3.Pin_2
  N6: SparkFun_Pro_Micro1.D3, S2.Pin_1, S2.Pin_2
  N7: SparkFun_Pro_Micro1.D2, S1.Pin_1, S1.Pin_2
  N8: SparkFun_Pro_Micro1.GND, LED1.C, LED2.C, LED3.C, LED4.C, LED5.C, LED6.C, S1.Pin_3, S1.Pin_4, S2.Pin_3, S2.Pin_4, S3.Pin_3, S3.Pin_4, S4.Pin_3, S4.Pin_4, S5.Pin_3, S5.Pin_4, S6.Pin_3, S6.Pin_4

custom parts:
  SparkFun Pro Micro: This tiny little board does all of the neat-o Arduino tricks that you’re familiar with: 4 channels of 10-bit ADC, 5 PWM pins, 12 DIOs as well as hardware serial connections Rx and Tx. Running at 16MHz and 5V, this board will remind you a lot of your other favorite Arduino-compatible boards but this little guy can go just about anywhere. There is a voltage regulator on board so it can accept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
  Pushbutton: A generic pushbutton. This is a standard 12mm square momentary button. What we really like is the large button head and good tactile feel (it ‘clicks’ really well). This button is great for user input on a PCB or a good, big reset button on a breadboard. Breadboard friendly! SparkFun Storefront SKU: COM-09190 Modified by: Ho Yun "Bobby" Chan @ SparkFun Electronics Inc.
